# Fritzing sketch esp8266_sensors (saved by Fritzing 0.9.3b)
circuit board: 5.39655cm x 5.03191cm
perfboards: 1

parts:
  J2 = female pin header, 11 pins [form="♀ (female)"]
  IC1 = Voltage Regulator [package=to-92]
  S2 = Pushbutton [package="[THT]"]
  J1 = female pin header, 11 pins [form="♀ (female)"]
  J5 = male pin header, 2 pins [form="♂ (male)"]
  J4 = female pin header, 6 pins [form="♀ (female)"]
  R2 = Resistor [tolerance=±5% resistance=10k package=THT]
  R3 = Resistor [tolerance=±5% resistance=10k package=THT]
  J10 = Screw terminal - 2 pins [package=THT]
  R4 = Resistor [tolerance=±5% resistance=330k package=THT]
  R5 = Resistor [tolerance=±5% resistance=47k package=THT]
  J11 = male pin header, 2 pins [form="♂ (male)"]
  C1 = Tantalum Capacitor [capacitance=2.2µF package="100 mil [THT, tantalum]"]
  C2 = Tantalum Capacitor [capacitance=2.2µF package="100 mil [THT, tantalum]"]
  U5 = mystery part, 6 pins [chip_label=?]
  U6 = mystery part, 6 pins [chip_label=?]
  U7 = mystery part, 6 pins [chip_label=?]
  U8 = mystery part, 6 pins [chip_label=?]
  U9 = mystery part, 6 pins [chip_label=?]
  U10 = mystery part, 6 pins [chip_label=?]
  J12 = female pin header, 10 pins [form="♀ (female)"]
  DHT1 = DHT22_Humidity_and_Temperature_Sensor
  R1 = Resistor [tolerance=±5% resistance=10k package=THT]

nets:
  N1: J2.pin1, R2.Pin_1, J12.pin7
  N2: J2.pin2, J12.pin6
  N3: J2.pin3, J12.pin5
  N4: J2.pin4, J12.pin4
  N5: J2.pin5, J12.pin3, DHT1.connector2, R1.Pin_0
  N6: J2.pin6, J12.pin2
  N7: J2.pin7, J12.pin1
  N8: J2.pin8, J5.pin1
  N9: J2.pin10, S2.Pin_3, S2.Pin_4, J5.pin2
  N10: J2.pin11, J11.pin2
  N11: IC1.GND, S2.Pin_1, S2.Pin_2, J1.pin2, J4.pin1, J10.pin1, R5.Pin_0, C1.-, C2.-, DHT1.connector4
  N12: IC1.IN, J10.pin2, R4.Pin_0, C2.+
  N13: IC1.OUT, J1.pin1, R2.Pin_0, R3.Pin_0, C1.+, J12.pin10, DHT1.connector1, R1.Pin_1
  N14: J1.pin3, J4.pin5
  N15: J1.pin4, J4.pin4
  N16: J1.pin11, R3.Pin_1, J12.pin8
  N17: R4.Pin_1, R5.Pin_1, J11.pin1
  N18: U5.pin1, U5.pin2, U5.pin3
  N19: U5.pin4, U5.pin5, U5.pin6
  N20: U6.pin1, U6.pin2, U6.pin3
  N21: U6.pin4, U6.pin5, U6.pin6
  N22: U7.pin1, U7.pin2, U7.pin3
  N23: U7.pin4, U7.pin5, U7.pin6
  N24: U8.pin1, U8.pin2, U8.pin3
  N25: U8.pin4, U8.pin5, U8.pin6
  N26: U9.pin1, U9.pin2, U9.pin3
  N27: U9.pin4, U9.pin5, U9.pin6
  N28: U10.pin1, U10.pin2, U10.pin3
  N29: U10.pin4, U10.pin5, U10.pin6

notes:
  GND
  CTS
  POWER
  TXO
  RXI
  DTR
  GPIO1: U0TXD -> RXI
  GPIO3: U0RXD -> TXO
  RESET
  IC1: MCP1700-3302E/TO
  C1 and C2: 2.2µF
  Prototype Area
  I2C: GPIO4/22 -> SDA, GPIO5/11 -> SCL
